// Digital circuit 4-bit-processor.dig as structural Verilog
module _4_bit_processor (
  input  Clock,
  input  [1:0] IR_Ctrl,
  input  [1:0] inte_mem_ctrl,
  input  [3:0] Mem_input,
  input  [1:0] PC_ctrl,
  output [3:0] data_read_1,
  output [3:0] data_read_2,
  output [3:0] ALU_out,
  output [15:0] Instruct_out
);

  wire data_path_4_bit_processor_1_enable_alu;
  wire [7:0] multiplexer_1_out, registerfile_write_ctrl_1_write_ctr;

  data_path_4_bit_processor data_path_4_bit_processor_1 (
    .Clock(Clock), .IR_Ctrl(IR_Ctrl), .pc_ctrl(PC_ctrl), .intr_Mem_ctrl(inte_mem_ctrl),
    .intr_mem_input(Mem_input), .ir_output(Instruct_out), .Enable_AlU(data_path_4_bit_processor_1_enable_alu));
  RegisterFile_Write_ctrl registerfile_write_ctrl_1 (
    .OpCode3(Instruct_out[1:0]), .Write_ctr(registerfile_write_ctrl_1_write_ctr));
  Multiplexer #(.Bits(8)) multiplexer_1 (
    .sel(data_path_4_bit_processor_1_enable_alu), .in_0(registerfile_write_ctrl_1_write_ctr),
    .in_1({8{1'b0}}), .out(multiplexer_1_out));
  // registers_file registers_file_1: pin names not known; wires that end beside it: Instruct_out[5:4], Instruct_out[3:2], Clock, ALU_out, Instruct_out[1:0], multiplexer_1_out, data_read_1, data_read_2
  ALU_4_Bit alu_4_bit_1 (.A(data_read_1), .B(data_read_2), .S_1_S_0_C_in(Instruct_out[8:6]), .D(ALU_out));

  // Notes on the sheet:
  //   PC_ctrl: default 1
endmodule

/* Test case test-4-bit-processor:
Clock IR_Ctrl inte-mem-ctrl Mem_input PC_ctrl Instruct-out data-read-1 data-read-2 ALU-out
c 0 1 0 1 x x x x
c 0 1 4 1 x x x x
c 0 1 1 1 x x x x
c 0 1 0 1 x x x x
c 0 1 1 1 x x x x
c 0 1 5 1 x x x x
c 0 1 1 1 x x x x
c 0 1 0 1 x x x x
c 0 1 9 1 x x x x
c 0 1 10 1 x x x x
c 0 1 11 1 x x x x
c 0 1 12 1 x x x x
c 0 1 13 1 x x x x
c 0 1 14 1 x x x x
c 0 1 15 1 x x x x
c 1 0 1 1 x x x x
c 1 0 1 1 x x x x
c 1 0 1 1 x x x x
c 1 0 1 1 x x x x
c 1 0 1 1 x x x x
c 1 0 1 1 x x x x
c 0 1 0 1 x x x x
c 1 0 1 1 x x x x
c 1 0 1 1 x x x x
c 1 0 1 1 x x x x
c 1 0 1 1 x x x x
c 1 0 1 1 x x x x
c 1 0 1 1 x x x x
c 1 0 1 1 x x x x
c 1 0 1 1 x x x x
c 1 0 1 1 x x x x
c 1 0 1 1 x x x x
c 1 0 1 1 x x x x
c 1 0 1 1 x x x x
c 0 1 0 1 x x x x
c 1 0 1 1 x x x x
c 1 0 1 1 x x x x
c 1 0 1 1 x x x x
c 1 0 1 1 x x x x
c 1 0 1 1 x x x x
c 1 0 1 1 x x x x
*/
