// Digital circuit Data-Path-Pro-Counter.dig as structural Verilog
module Data_Path_Pro_Counter (
  input  [1:0] CTRL,
  input  CLK,
  output [3:0] X
);

  wire [3:0] _4_bit_adder_1_p3, multiplexer_1_out, not_1_out;

  // _4_bit_Adder _4_bit_adder_1: pin names not known; wires that end beside it: X, 4'b0001, _4_bit_adder_1_p3
  assign not_1_out = ~4'b0000;  // Not not_1, 4 bits wide
  Multiplexer #(.Selector_Bits(2), .Bits(4)) multiplexer_1 (
    .sel(CTRL), .in_0(X), .in_1(_4_bit_adder_1_p3), .in_2(4'b0000), .in_3(not_1_out), .out(multiplexer_1_out));
  D_FF d_ff_1 (.D(multiplexer_1_out[3]), .C(CLK), .Q(X[3]));  // open: nQ
  D_FF d_ff_2 (.D(multiplexer_1_out[2]), .C(CLK), .Q(X[2]));  // open: nQ
  D_FF d_ff_3 (.D(multiplexer_1_out[1]), .C(CLK), .Q(X[1]));  // open: nQ
  D_FF d_ff_4 (.D(multiplexer_1_out[0]), .C(CLK), .Q(X[0]));  // open: nQ
endmodule
