// Digital circuit RegisterFile_Write_ctrl.dig as structural Verilog
module RegisterFile_Write_ctrl (
  input  [1:0] OpCode3,
  output [7:0] Write_ctr
);

  Decoder #(.Selector_Bits(2)) decoder_1 (
    .sel(OpCode3), .out_0(Write_ctr[0]), .out_1(Write_ctr[2]), .out_2(Write_ctr[4]), .out_3(Write_ctr[6]));

  assign {Write_ctr[7], Write_ctr[5], Write_ctr[3], Write_ctr[1]} = 4'b0000;
endmodule
