// Digital circuit data-path-4-bit-processor.dig as structural Verilog
module data_path_4_bit_processor (
  input  Clock,
  input  [1:0] IR_Ctrl,
  input  [1:0] pc_ctrl,
  input  [1:0] intr_Mem_ctrl,
  input  [3:0] intr_mem_input,
  output [15:0] ir_output,
  output Enable_AlU
);

  wire not_1_out, not_2_out;
  wire [1:0] demultiplexer_1_out_0, demultiplexer_1_out_1, demultiplexer_1_out_2, demultiplexer_1_out_3;
  wire [3:0] _4_bit_16_address_dram_1_output, _4_bit_instruction_register_1_output,
       _4_bit_instruction_register_2_output, _4_bit_instruction_register_3_output,
       _4_bit_instruction_register_4_output, data_path_pro_counter_1_x, demultiplexer_2_out_0,
       demultiplexer_2_out_1, demultiplexer_2_out_2, demultiplexer_2_out_3;

  Data_Path_Pro_Counter data_path_pro_counter_1 (.CTRL(pc_ctrl), .CLK(Clock), .X(data_path_pro_counter_1_x));
  _4_bit_16_address_Dram _4_bit_16_address_dram_1 (
    .Address(data_path_pro_counter_1_x), .Input(intr_mem_input), .CTRL(intr_Mem_ctrl), .Clock(Clock),
    .Output(_4_bit_16_address_dram_1_output));
  Demultiplexer #(.Selector_Bits(2), .Bits(2)) demultiplexer_1 (
    .sel(data_path_pro_counter_1_x[1:0]), .in(IR_Ctrl), .out_0(demultiplexer_1_out_0),
    .out_1(demultiplexer_1_out_1), .out_2(demultiplexer_1_out_2), .out_3(demultiplexer_1_out_3));
  Demultiplexer #(.Selector_Bits(2), .Bits(4)) demultiplexer_2 (
    .sel(data_path_pro_counter_1_x[1:0]), .in(_4_bit_16_address_dram_1_output),
    .out_0(demultiplexer_2_out_0), .out_1(demultiplexer_2_out_1), .out_2(demultiplexer_2_out_2),
    .out_3(demultiplexer_2_out_3));
  not not_1 (not_1_out, data_path_pro_counter_1_x[2]);
  not not_2 (not_2_out, data_path_pro_counter_1_x[3]);
  and and_1 (Enable_AlU, not_1_out, not_2_out);
  _4_bit_instruction_register _4_bit_instruction_register_1 (
    .clk(Clock), .CTRL(demultiplexer_1_out_0), .Input(demultiplexer_2_out_0),
    .Output(_4_bit_instruction_register_1_output));
  _4_bit_instruction_register _4_bit_instruction_register_2 (
    .clk(Clock), .CTRL(demultiplexer_1_out_1), .Input(demultiplexer_2_out_1),
    .Output(_4_bit_instruction_register_2_output));
  _4_bit_instruction_register _4_bit_instruction_register_3 (
    .clk(Clock), .CTRL(demultiplexer_1_out_2), .Input(demultiplexer_2_out_2),
    .Output(_4_bit_instruction_register_3_output));
  _4_bit_instruction_register _4_bit_instruction_register_4 (
    .clk(Clock), .CTRL(demultiplexer_1_out_3), .Input(demultiplexer_2_out_3),
    .Output(_4_bit_instruction_register_4_output));
  assign ir_output = Enable_AlU ? {_4_bit_instruction_register_4_output, _4_bit_instruction_register_3_output, _4_bit_instruction_register_2_output, _4_bit_instruction_register_1_output} : 16'bz;  // Driver driver_1

  // Notes on the sheet:
  //   pc_ctrl: default 1
endmodule
